// Digital circuit 3x8 Decoder with 0-Enable.dig as structural Verilog
module _3x8_Decoder_with_0_Enable (
  input  X,
  input  Y,
  input  Z,
  input  En,
  output F0,
  output F1,
  output F2,
  output F3,
  output F4,
  output F5,
  output F6,
  output F7
);

  wire not_1_out, not_2_out, not_3_out, not_4_out;

  not not_1 (not_1_out, X);
  not not_2 (not_2_out, Y);
  not not_3 (not_3_out, Z);
  not not_4 (not_4_out, En);
  and and_1 (F0, not_1_out, not_2_out, not_3_out, not_4_out);
  and and_2 (F1, not_1_out, not_2_out, Z, not_4_out);
  and and_3 (F2, not_1_out, Y, not_3_out, not_4_out);
  and and_4 (F3, not_1_out, Y, Z, not_4_out);
  and and_5 (F4, X, not_2_out, not_3_out, not_4_out);
  and and_6 (F5, X, not_2_out, Z, not_4_out);
  and and_7 (F6, X, Y, not_3_out, not_4_out);
  and and_8 (F7, X, Y, Z, not_4_out);
endmodule
