// Digital circuit Active Low 4x16 Decoder.dig as structural Verilog
module Active_Low_4x16_Decoder (
  input  S3,
  input  S2,
  input  S1,
  input  S0,
  output F0,
  output F1,
  output F2,
  output F3,
  output F4,
  output F5,
  output F6,
  output F7,
  output F8,
  output F9,
  output F10,
  output F11,
  output F12,
  output F13,
  output F14,
  output F15
);

  wire _3x8_decoder_with_1_enable_1_f0, _3x8_decoder_with_1_enable_1_f1, _3x8_decoder_with_1_enable_1_f2,
       _3x8_decoder_with_1_enable_1_f3, _3x8_decoder_with_1_enable_1_f4, _3x8_decoder_with_1_enable_1_f5,
       _3x8_decoder_with_1_enable_1_f6, _3x8_decoder_with_1_enable_1_f7, _3x8_decoder_with_1_enable_2_f0,
       _3x8_decoder_with_1_enable_2_f1, _3x8_decoder_with_1_enable_2_f2, _3x8_decoder_with_1_enable_2_f3,
       _3x8_decoder_with_1_enable_2_f4, _3x8_decoder_with_1_enable_2_f5, _3x8_decoder_with_1_enable_2_f6,
       _3x8_decoder_with_1_enable_2_f7, not_1_out;

  not not_1 (not_1_out, S3);
  _3x8_Decoder_with_1_Enable _3x8_decoder_with_1_enable_1 (
    .X(S2), .Y(S1), .Z(S0), .En(not_1_out), .F0(_3x8_decoder_with_1_enable_1_f0),
    .F1(_3x8_decoder_with_1_enable_1_f1), .F2(_3x8_decoder_with_1_enable_1_f2),
    .F3(_3x8_decoder_with_1_enable_1_f3), .F4(_3x8_decoder_with_1_enable_1_f4),
    .F5(_3x8_decoder_with_1_enable_1_f5), .F6(_3x8_decoder_with_1_enable_1_f6),
    .F7(_3x8_decoder_with_1_enable_1_f7));
  _3x8_Decoder_with_1_Enable _3x8_decoder_with_1_enable_2 (
    .X(S2), .Y(S1), .Z(S0), .En(S3), .F0(_3x8_decoder_with_1_enable_2_f0),
    .F1(_3x8_decoder_with_1_enable_2_f1), .F2(_3x8_decoder_with_1_enable_2_f2),
    .F3(_3x8_decoder_with_1_enable_2_f3), .F4(_3x8_decoder_with_1_enable_2_f4),
    .F5(_3x8_decoder_with_1_enable_2_f5), .F6(_3x8_decoder_with_1_enable_2_f6),
    .F7(_3x8_decoder_with_1_enable_2_f7));
  not not_2 (F0, _3x8_decoder_with_1_enable_1_f0);
  not not_3 (F1, _3x8_decoder_with_1_enable_1_f1);
  not not_4 (F2, _3x8_decoder_with_1_enable_1_f2);
  not not_5 (F3, _3x8_decoder_with_1_enable_1_f3);
  not not_6 (F4, _3x8_decoder_with_1_enable_1_f4);
  not not_7 (F5, _3x8_decoder_with_1_enable_1_f5);
  not not_8 (F6, _3x8_decoder_with_1_enable_1_f6);
  not not_9 (F7, _3x8_decoder_with_1_enable_1_f7);
  not not_10 (F8, _3x8_decoder_with_1_enable_2_f0);
  not not_11 (F9, _3x8_decoder_with_1_enable_2_f1);
  not not_12 (F10, _3x8_decoder_with_1_enable_2_f2);
  not not_13 (F11, _3x8_decoder_with_1_enable_2_f3);
  not not_14 (F12, _3x8_decoder_with_1_enable_2_f4);
  not not_15 (F13, _3x8_decoder_with_1_enable_2_f5);
  not not_16 (F14, _3x8_decoder_with_1_enable_2_f6);
  not not_17 (F15, _3x8_decoder_with_1_enable_2_f7);
endmodule
