// Digital circuit Use Decoder.dig as structural Verilog
module Use_Decoder (
  input  P,
  input  Q,
  input  R,
  input  S,
  output F
);

  wire active_low_4x16_decoder_1_f1, active_low_4x16_decoder_1_f2, active_low_4x16_decoder_1_f3,
       active_low_4x16_decoder_1_f5, active_low_4x16_decoder_1_f8, active_low_4x16_decoder_1_f13;

  Active_Low_4x16_Decoder active_low_4x16_decoder_1 (
    .S3(P), .S2(Q), .S1(R), .S0(S), .F1(active_low_4x16_decoder_1_f1), .F2(active_low_4x16_decoder_1_f2),
    .F3(active_low_4x16_decoder_1_f3), .F5(active_low_4x16_decoder_1_f5), .F8(active_low_4x16_decoder_1_f8),
    .F13(active_low_4x16_decoder_1_f13));  // open: F0, F4, F6, F7, F9, F10, F11, F12, F14, F15
  nand nand_1 (F, active_low_4x16_decoder_1_f1, active_low_4x16_decoder_1_f2, active_low_4x16_decoder_1_f3, active_low_4x16_decoder_1_f5, active_low_4x16_decoder_1_f8, active_low_4x16_decoder_1_f13);
endmodule
