// Digital circuit Use Multiplexer 3a.dig as structural Verilog
module Use_Multiplexer_3a (
  input  P,
  input  Q,
  input  R,
  input  S,
  output F
);

  wire not_1_out, not_2_out, not_3_out;

  not not_1 (not_1_out, P);
  not not_2 (not_2_out, P);
  not not_3 (not_3_out, P);
  Multiplexer #(.Selector_Bits(3)) multiplexer_1 (
    .sel({Q, R, S}), .in_0(P), .in_1(not_1_out), .in_2(not_2_out), .in_3(not_3_out), .in_4(1'b0),
    .in_5(1'b1), .in_6(1'b0), .in_7(1'b0), .out(F));

  // Notes on the sheet:
  //   These are the selector bits.
endmodule
