// Digital circuit Use Multiplexer 3b.dig as structural Verilog
module Use_Multiplexer_3b (
  input  P,
  input  Q,
  input  R,
  input  S,
  output F
);

  wire not_1_out;

  not not_1 (not_1_out, S);
  Multiplexer #(.Selector_Bits(3)) multiplexer_1 (
    .sel({P, Q, R}), .in_0(S), .in_1(1'b1), .in_2(S), .in_3(1'b0), .in_4(not_1_out), .in_5(1'b0), .in_6(S),
    .in_7(1'b0), .out(F));

  // Notes on the sheet:
  //   These are the selector bits.
endmodule
