// Digital circuit Use Multiplexer.dig as structural Verilog
module Use_Multiplexer (
  input  P,
  input  Q,
  input  R,
  input  S,
  output F
);

  Multiplexer #(.Selector_Bits(3)) multiplexer_1 (.sel({Q, R, S}));  // open: in_0, in_1, in_2, in_3, in_4, in_5, in_6, in_7, out

  // Notes on the sheet:
  //   These are the selector bits.
endmodule
