// Digital circuit SimplifiedPrime.dig as structural Verilog
module SimplifiedPrime (
  input  a,
  input  b,
  input  c,
  output \output 
);

  wire and_1_out, and_2_out, not_1_out;

  and and_1 (and_1_out, not_1_out, b);
  not not_1 (not_1_out, a);
  and and_2 (and_2_out, a, c);
  or or_1 (\output , and_1_out, and_2_out);
endmodule
