// Digital circuit 4-bit Cascade Adder.dig as structural Verilog
module _4_bit_Cascade_Adder (
  input  X0,
  input  X1,
  input  X2,
  input  X3,
  input  Y0,
  input  Y1,
  input  Y2,
  input  Y3,
  input  C0,
  output C4,
  output S0,
  output S1,
  output S2,
  output S3
);

  wire full_adder_1_carry, full_adder_2_carry, full_adder_3_carry;

  Full_Adder full_adder_1 (.X(X0), .Y(Y0), .Z(C0), .Sum(S0), .Carry(full_adder_1_carry));
  Full_Adder full_adder_2 (.X(X1), .Y(Y1), .Z(full_adder_1_carry), .Sum(S1), .Carry(full_adder_2_carry));
  Full_Adder full_adder_3 (.X(X2), .Y(Y2), .Z(full_adder_2_carry), .Sum(S2), .Carry(full_adder_3_carry));
  Full_Adder full_adder_4 (.X(X3), .Y(Y3), .Z(full_adder_3_carry), .Sum(S3), .Carry(C4));
endmodule
