// Digital circuit Full Adder.dig as structural Verilog
module Full_Adder (
  input  X,
  input  Y,
  input  Z,
  output Sum,
  output Carry
);

  wire half_adder_1_carry, half_adder_1_sum, half_adder_2_carry;

  Half_Adder half_adder_1 (.X(X), .Y(Y), .Sum(half_adder_1_sum), .Carry(half_adder_1_carry));
  Half_Adder half_adder_2 (.X(half_adder_1_sum), .Y(Z), .Sum(Sum), .Carry(half_adder_2_carry));
  or or_1 (Carry, half_adder_1_carry, half_adder_2_carry);
endmodule
