// Digital circuit Lab 09 - Multiply by 6.dig as structural Verilog
module Lab_09___Multiply_by_6 (
  input  A,
  input  B,
  input  C,
  output [4:0] S,
  output V
);

  _4_bit_Cascade_Adder _4_bit_cascade_adder_1 (
    .X0(C), .X1(B), .X2(A), .X3(1'b0), .Y0(1'b0), .Y1(C), .Y2(B), .Y3(A), .C0(1'b0), .S0(S[1]), .S1(S[2]),
    .S2(S[3]), .S3(S[4]));  // open: C4
  nand nand_1 (V, B, A);

  assign S[0] = 1'b0;
endmodule
